// Logisim project lab03_2019_11_28_0915_v_2019_12_02_2358.circ as structural Verilog: 8 circuits, main circuit main
module main (
  input  [31:0] in_1,
  input  in_2,
  input  in_3,
  input  in_4,
  input  in_5,
  input  in_6,
  input  RegDst,
  input  in_8,
  input  [2:0] in_9,
  input  MemtoReg,
  input  [31:0] in_11,
  input  in_12,
  input  in_13
);

  wire [4:0] multiplexer_1_out, undriven_5, undriven_6, undriven_7;
  wire [31:0] adder_1_out, adder_2_out, multiplexer_2_out, multiplexer_3_out, undriven, undriven_2,
       undriven_3, undriven_4;

  PC pc_1 (.Q(undriven), .D(multiplexer_2_out), .write(in_3), .CLK(in_5));
  InstructionMemory instructionmemory_1 (.Read_Address(undriven), .Instructions_32(undriven_2));
  ALU alu_1 (.in_01(undriven_3), .in_02(undriven_4), .ALU_result(multiplexer_3_out), .zero_output(in_8), .ALU_OP(in_9));
  Adder #(.width(32)) adder_1 (.a(undriven), .b(in_1), .out(adder_1_out));  // open: cin, cout
  spliter spliter_1 (
    .inst31_0(undriven_2), .inst20_16(undriven_5), .inst25_21(undriven_6), .inst15_11(undriven_7));  // open: inst15_0, inst5_0
  Multiplexer #(.width(5), .enable("false")) multiplexer_1 (
    .in0(undriven_5), .in1(undriven_7), .out(multiplexer_1_out), .sel(RegDst));
  Adder #(.width(32)) adder_2 (.a(adder_1_out), .out(adder_2_out));  // open: b, cin, cout
  memoria_4_x_8 DATA_MEMORY (
    .ADDRESS(multiplexer_3_out), .Read_data(in_11), .Write_data(undriven_4), .MemWrite(in_12),
    .MemRead(in_13), .CLK(in_5));  // open: whb
  Multiplexer #(.width(32), .enable("false")) multiplexer_2 (
    .in0(adder_1_out), .in1(adder_2_out), .out(multiplexer_2_out), .sel(in_2));
  Multiplexer #(.width(32), .enable("false")) multiplexer_3 (
    .in0(multiplexer_3_out), .in1(in_11), .out(multiplexer_3_out), .sel(MemtoReg));
  registers Register_ (
    .Read_register_1(undriven_6), .Read_register_2(undriven_5), .alway_zero(in_4), .Read_data_1(undriven_3),
    .Read_data_2(undriven_4), .Write_data(multiplexer_3_out), .CLK(in_5), .enable_write(in_6),
    .Write_register(multiplexer_1_out));

  // Notes on the sheet:
  //   spliter - Emaranhado de fios para barramento
endmodule

module ALU (
  input  [31:0] in_01,
  input  [31:0] in_02,
  input  [31:0] ALU_result,
  input  zero_output,
  input  [2:0] ALU_OP
);

  wire or_2_out;
  wire [31:0] adder_1_out, and_1_out, nor_1_out, or_1_out, subtractor_1_out;

  Adder #(.width(32)) adder_1 (.a(in_01), .b(in_02), .out(adder_1_out));  // open: cin, cout
  Subtractor #(.width(32)) subtractor_1 (.a(in_01), .b(in_02), .out(subtractor_1_out));  // open: bin, bout
  assign and_1_out = in_01 & in_02;  // AND_Gate and_1, 32 bits wide
  assign or_1_out = in_01 | in_02;  // OR_Gate or_1, 32 bits wide
  assign nor_1_out = ~(in_01 | in_02);  // NOR_Gate nor_1, 32 bits wide
  Multiplexer #(.select(3), .width(32), .enable("false")) multiplexer_1 (
    .in0(adder_1_out), .in1(subtractor_1_out), .in2(and_1_out), .in3(or_1_out), .in4(nor_1_out),
    .out(ALU_result), .sel(ALU_OP));  // open: in5, in6, in7
  or or_2 (or_2_out, ALU_result[0], ALU_result[1], ALU_result[2], ALU_result[3], ALU_result[4], ALU_result[5], ALU_result[6], ALU_result[7], ALU_result[8], ALU_result[9], ALU_result[10], ALU_result[11], ALU_result[12], ALU_result[13], ALU_result[14], ALU_result[15], ALU_result[17], ALU_result[18], ALU_result[19], ALU_result[20], ALU_result[21], ALU_result[22], ALU_result[23], ALU_result[24], ALU_result[25], ALU_result[26], ALU_result[27], ALU_result[28], ALU_result[29], ALU_result[30], ALU_result[31], ALU_result[16]);
  not not_1 (zero_output, or_2_out);
endmodule

module registers (
  input  [4:0] Read_register_1,
  input  [4:0] Read_register_2,
  input  alway_zero,
  input  [31:0] Read_data_1,
  input  [31:0] Read_data_2,
  input  [31:0] Write_data,
  input  CLK,
  input  enable_write,
  input  [4:0] Write_register
);

  wire demultiplexer_1_out0, demultiplexer_1_out1, demultiplexer_1_out2, demultiplexer_1_out3,
       demultiplexer_1_out4, demultiplexer_1_out5, demultiplexer_1_out6, demultiplexer_1_out7,
       demultiplexer_1_out8, demultiplexer_1_out9, demultiplexer_1_out10, demultiplexer_1_out11,
       demultiplexer_1_out12, demultiplexer_1_out13, demultiplexer_1_out14, demultiplexer_1_out15,
       demultiplexer_1_out16, demultiplexer_1_out17, demultiplexer_1_out18, demultiplexer_1_out19,
       demultiplexer_1_out20, demultiplexer_1_out21, demultiplexer_1_out22, demultiplexer_1_out23,
       demultiplexer_1_out24, demultiplexer_1_out25, demultiplexer_1_out26, demultiplexer_1_out27,
       demultiplexer_1_out28, demultiplexer_1_out29, demultiplexer_1_out30, demultiplexer_1_out31;
  wire [31:0] register_1_q, register_2_q, register_3_q, register_4_q, register_5_q, register_6_q,
       register_7_q, register_8_q, register_9_q, register_10_q, register_11_q, register_12_q, register_13_q,
       register_14_q, register_15_q, register_16_q, register_17_q, register_18_q, register_19_q,
       register_20_q, register_21_q, register_22_q, register_23_q, register_24_q, register_25_q,
       register_26_q, register_27_q, register_28_q, register_29_q, register_30_q, register_31_q,
       register_32_q;

  Demultiplexer #(.select(5), .enable("false")) demultiplexer_1 (
    .out0(demultiplexer_1_out0), .out1(demultiplexer_1_out1), .out2(demultiplexer_1_out2),
    .out3(demultiplexer_1_out3), .out4(demultiplexer_1_out4), .out5(demultiplexer_1_out5),
    .out6(demultiplexer_1_out6), .out7(demultiplexer_1_out7), .out8(demultiplexer_1_out8),
    .out9(demultiplexer_1_out9), .out10(demultiplexer_1_out10), .out11(demultiplexer_1_out11),
    .out12(demultiplexer_1_out12), .out13(demultiplexer_1_out13), .out14(demultiplexer_1_out14),
    .out15(demultiplexer_1_out15), .out16(demultiplexer_1_out16), .out17(demultiplexer_1_out17),
    .out18(demultiplexer_1_out18), .out19(demultiplexer_1_out19), .out20(demultiplexer_1_out20),
    .out21(demultiplexer_1_out21), .out22(demultiplexer_1_out22), .out23(demultiplexer_1_out23),
    .out24(demultiplexer_1_out24), .out25(demultiplexer_1_out25), .out26(demultiplexer_1_out26),
    .out27(demultiplexer_1_out27), .out28(demultiplexer_1_out28), .out29(demultiplexer_1_out29),
    .out30(demultiplexer_1_out30), .out31(demultiplexer_1_out31), .in(enable_write), .sel(Write_register));
  Register #(.width(32)) register_1 (
    .D(Write_data), .en(demultiplexer_1_out0), .clk(CLK), .Q(register_1_q), .clr(alway_zero));
  Register #(.width(32)) register_2 (
    .D(Write_data), .en(demultiplexer_1_out1), .clk(CLK), .Q(register_2_q), .clr(1'b0));
  Register #(.width(32)) register_3 (
    .D(Write_data), .en(demultiplexer_1_out2), .clk(CLK), .Q(register_3_q), .clr(1'b0));
  Register #(.width(32)) register_4 (
    .D(Write_data), .en(demultiplexer_1_out3), .clk(CLK), .Q(register_4_q), .clr(1'b0));
  Register #(.width(32)) register_5 (
    .D(Write_data), .en(demultiplexer_1_out4), .clk(CLK), .Q(register_5_q), .clr(1'b0));
  Register #(.width(32)) register_6 (
    .D(Write_data), .en(demultiplexer_1_out5), .clk(CLK), .Q(register_6_q), .clr(1'b0));
  Register #(.width(32)) register_7 (
    .D(Write_data), .en(demultiplexer_1_out6), .clk(CLK), .Q(register_7_q), .clr(1'b0));
  Register #(.width(32)) register_8 (
    .D(Write_data), .en(demultiplexer_1_out7), .clk(CLK), .Q(register_8_q), .clr(1'b0));
  Register #(.width(32)) register_9 (
    .D(Write_data), .en(demultiplexer_1_out8), .clk(CLK), .Q(register_9_q), .clr(1'b0));
  Register #(.width(32)) register_10 (
    .D(Write_data), .en(demultiplexer_1_out9), .clk(CLK), .Q(register_10_q), .clr(1'b0));
  Register #(.width(32)) register_11 (
    .D(Write_data), .en(demultiplexer_1_out10), .clk(CLK), .Q(register_11_q), .clr(1'b0));
  Register #(.width(32)) register_12 (
    .D(Write_data), .en(demultiplexer_1_out11), .clk(CLK), .Q(register_12_q), .clr(1'b0));
  Register #(.width(32)) register_13 (
    .D(Write_data), .en(demultiplexer_1_out12), .clk(CLK), .Q(register_13_q), .clr(1'b0));
  Register #(.width(32)) register_14 (
    .D(Write_data), .en(demultiplexer_1_out13), .clk(CLK), .Q(register_14_q), .clr(1'b0));
  Register #(.width(32)) register_15 (
    .D(Write_data), .en(demultiplexer_1_out14), .clk(CLK), .Q(register_15_q), .clr(1'b0));
  Register #(.width(32)) register_16 (
    .D(Write_data), .en(demultiplexer_1_out15), .clk(CLK), .Q(register_16_q), .clr(1'b0));
  Register #(.width(32)) register_17 (
    .D(Write_data), .en(demultiplexer_1_out16), .clk(CLK), .Q(register_17_q), .clr(1'b0));
  Register #(.width(32)) register_18 (
    .D(Write_data), .en(demultiplexer_1_out17), .clk(CLK), .Q(register_18_q), .clr(1'b0));
  Register #(.width(32)) register_19 (
    .D(Write_data), .en(demultiplexer_1_out18), .clk(CLK), .Q(register_19_q), .clr(1'b0));
  Register #(.width(32)) register_20 (
    .D(Write_data), .en(demultiplexer_1_out19), .clk(CLK), .Q(register_20_q), .clr(1'b0));
  Register #(.width(32)) register_21 (
    .D(Write_data), .en(demultiplexer_1_out20), .clk(CLK), .Q(register_21_q), .clr(1'b0));
  Register #(.width(32)) register_22 (
    .D(Write_data), .en(demultiplexer_1_out21), .clk(CLK), .Q(register_22_q), .clr(1'b0));
  Register #(.width(32)) register_23 (
    .D(Write_data), .en(demultiplexer_1_out22), .clk(CLK), .Q(register_23_q), .clr(1'b0));
  Register #(.width(32)) register_24 (
    .D(Write_data), .en(demultiplexer_1_out23), .clk(CLK), .Q(register_24_q), .clr(1'b0));
  Register #(.width(32)) register_25 (
    .D(Write_data), .en(demultiplexer_1_out24), .clk(CLK), .Q(register_25_q), .clr(1'b0));
  Register #(.width(32)) register_26 (
    .D(Write_data), .en(demultiplexer_1_out25), .clk(CLK), .Q(register_26_q), .clr(1'b0));
  Register #(.width(32)) register_27 (
    .D(Write_data), .en(demultiplexer_1_out26), .clk(CLK), .Q(register_27_q), .clr(1'b0));
  Register #(.width(32)) register_28 (
    .D(Write_data), .en(demultiplexer_1_out27), .clk(CLK), .Q(register_28_q), .clr(1'b0));
  Register #(.width(32)) register_29 (
    .D(Write_data), .en(demultiplexer_1_out28), .clk(CLK), .Q(register_29_q), .clr(1'b0));
  Register #(.width(32)) register_30 (
    .D(Write_data), .en(demultiplexer_1_out29), .clk(CLK), .Q(register_30_q), .clr(1'b0));
  Register #(.width(32)) register_31 (
    .D(Write_data), .en(demultiplexer_1_out30), .clk(CLK), .Q(register_31_q), .clr(1'b0));
  Register #(.width(32)) register_32 (
    .D(Write_data), .en(demultiplexer_1_out31), .clk(CLK), .Q(register_32_q), .clr(1'b0));
  Multiplexer #(.select(5), .width(32), .enable("false")) multiplexer_1 (
    .in0(register_1_q), .in1(register_2_q), .in2(register_3_q), .in3(register_4_q), .in4(register_5_q),
    .in5(register_6_q), .in6(register_7_q), .in7(register_8_q), .in8(register_9_q), .in9(register_10_q),
    .in10(register_11_q), .in11(register_12_q), .in12(register_13_q), .in13(register_14_q),
    .in14(register_15_q), .in15(register_16_q), .in16(register_17_q), .in17(register_18_q),
    .in18(register_19_q), .in19(register_20_q), .in20(register_21_q), .in21(register_22_q),
    .in22(register_23_q), .in23(register_24_q), .in24(register_25_q), .in25(register_26_q),
    .in26(register_27_q), .in27(register_28_q), .in28(register_29_q), .in29(register_30_q),
    .in30(register_31_q), .in31(register_32_q), .out(Read_data_1), .sel(Read_register_1));
  Multiplexer #(.select(5), .width(32), .enable("false")) multiplexer_2 (
    .in0(register_1_q), .in1(register_2_q), .in2(register_3_q), .in3(register_4_q), .in4(register_5_q),
    .in5(register_6_q), .in6(register_7_q), .in7(register_8_q), .in8(register_9_q), .in9(register_10_q),
    .in10(register_11_q), .in11(register_12_q), .in12(register_13_q), .in13(register_14_q),
    .in14(register_15_q), .in15(register_16_q), .in16(register_17_q), .in17(register_18_q),
    .in18(register_19_q), .in19(register_20_q), .in20(register_21_q), .in21(register_22_q),
    .in22(register_23_q), .in23(register_24_q), .in24(register_25_q), .in25(register_26_q),
    .in26(register_27_q), .in27(register_28_q), .in28(register_29_q), .in29(register_30_q),
    .in30(register_31_q), .in31(register_32_q), .out(Read_data_2), .sel(Read_register_2));
endmodule

module memoria_4_x_8 (
  input  [31:0] ADDRESS,
  input  [31:0] Read_data,
  input  [31:0] Write_data,
  input  [1:0] whb,
  input  MemWrite,
  input  MemRead,
  input  CLK
);

  wire [1:0] demultiplexer_3_out0, demultiplexer_3_out1;
  wire [3:0] demultiplexer_4_out0, multiplexer_2_out;
  wire [7:0] demultiplexer_2_out0, demultiplexer_2_out1, demultiplexer_2_out2, demultiplexer_2_out3,
       multiplexer_4_out, ram_1_dout, ram_2_dout, ram_3_dout, ram_4_dout;
  wire [15:0] demultiplexer_1_out0, demultiplexer_1_out1, multiplexer_3_out;
  wire [31:0] multiplexer_1_out;

  Demultiplexer #(.width(16), .enable("false")) demultiplexer_1 (
    .out0(demultiplexer_1_out0), .out1(demultiplexer_1_out1), .in(Write_data[15:0]), .sel(ADDRESS[1]));
  Demultiplexer #(.select(2), .width(8), .enable("false")) demultiplexer_2 (
    .out0(demultiplexer_2_out0), .out1(demultiplexer_2_out1), .out2(demultiplexer_2_out2),
    .out3(demultiplexer_2_out3), .in(Write_data[7:0]), .sel(ADDRESS[1:0]));
  Demultiplexer #(.width(2), .enable("false")) demultiplexer_3 (
    .out0(demultiplexer_3_out0), .out1(demultiplexer_3_out1), .in({2{MemWrite}}), .sel(ADDRESS[1]));
  Demultiplexer #(.select(2), .enable("false")) demultiplexer_4 (
    .out0(demultiplexer_4_out0[0]), .out1(demultiplexer_4_out0[1]), .out2(demultiplexer_4_out0[2]),
    .out3(demultiplexer_4_out0[3]), .in(MemWrite), .sel(ADDRESS[1:0]));
  Multiplexer #(.select(2), .width(32), .enable("false")) multiplexer_1 (
    .in0(Write_data), .in1({demultiplexer_1_out1, demultiplexer_1_out0}),
    .in2({demultiplexer_2_out3, demultiplexer_2_out2, demultiplexer_2_out1, demultiplexer_2_out0}),
    .in3({32{1'b0}}), .out(multiplexer_1_out), .sel(whb));
  Multiplexer #(.select(2), .width(4), .enable("false")) multiplexer_2 (
    .in0({4{MemWrite}}), .in1({demultiplexer_3_out1, demultiplexer_3_out0}), .in2(demultiplexer_4_out0),
    .in3(4'b0000), .out(multiplexer_2_out), .sel(whb));
  RAM #(.addrWidth(24), .databus("bibus")) ram_1 (
    .addr(ADDRESS[25:2]), .we(multiplexer_2_out[0]), .oe(MemRead), .clk(CLK), .din(multiplexer_1_out[7:0]),
    .dout(ram_1_dout));
  RAM #(.addrWidth(24), .databus("bibus")) ram_2 (
    .addr(ADDRESS[25:2]), .we(multiplexer_2_out[1]), .oe(MemRead), .clk(CLK), .din(multiplexer_1_out[15:8]),
    .dout(ram_2_dout));
  RAM #(.addrWidth(24), .databus("bibus")) ram_3 (
    .addr(ADDRESS[25:2]), .we(multiplexer_2_out[2]), .oe(MemRead), .clk(CLK), .din(multiplexer_1_out[23:16]),
    .dout(ram_3_dout));
  RAM #(.addrWidth(24), .databus("bibus")) ram_4 (
    .addr(ADDRESS[25:2]), .we(multiplexer_2_out[3]), .oe(MemRead), .clk(CLK), .din(multiplexer_1_out[31:24]),
    .dout(ram_4_dout));
  Multiplexer #(.width(16), .enable("false")) multiplexer_3 (
    .in0({ram_2_dout, ram_1_dout}), .in1({ram_4_dout, ram_3_dout}), .out(multiplexer_3_out), .sel(ADDRESS[1]));
  Multiplexer #(.select(2), .width(8), .enable("false")) multiplexer_4 (
    .in0(ram_1_dout), .in1(ram_2_dout), .in2(ram_3_dout), .in3(ram_4_dout), .out(multiplexer_4_out),
    .sel(ADDRESS[1:0]));
  Multiplexer #(.select(2), .width(32), .enable("false")) multiplexer_5 (
    .in0({ram_4_dout, ram_3_dout, ram_2_dout, ram_1_dout}), .in1({{16{1'b0}}, multiplexer_3_out}),
    .in2({{24{1'b0}}, multiplexer_4_out}), .in3({32{1'b0}}), .out(Read_data), .sel(whb));

  // Notes on the sheet:
  //   a0
  //   a0
  //   a0
  //   a1
  //   a1
  //   a1
  //   a2 - a26
  //   d0 - d31
  //   d0 - d15
  //   do - d7
  //   a1
  //   a1
  //   a0-a1
  //   a1
  //   a1
  //   a1
  //   a0
  //   a0-a1
  //   sinal whb seleciona byte half ou word da memoria
endmodule

module InstructionMemory (
  input  [31:0] Read_Address,
  input  [31:0] Instructions_32
);

  RAM #(.addrWidth(24), .dataWidth(32)) ram_1 (.addr(Read_Address[25:2]), .data(Instructions_32));  // open: we, oe, clk
endmodule

module PC (
  input  [31:0] Q,
  input  [31:0] D,
  input  write,
  input  CLK
);

  Register #(.width(32)) register_1 (.D(D), .en(write), .clk(CLK), .Q(Q), .clr(1'b0));
endmodule

module spliter (
  input  [31:0] inst31_0,
  input  [15:0] inst15_0,
  input  [4:0] inst20_16,
  input  [4:0] inst25_21,
  input  [4:0] inst5_0,
  input  [4:0] inst15_11
);


  assign inst15_0[4:0] = inst5_0;
  assign inst15_11 = inst15_0[15:11];
  assign inst31_0[25:0] = {inst25_21, inst20_16, inst15_0[15:5], inst5_0};

  // Notes on the sheet:
  //   Instruction [15-0]
  //   Instruction [5-0]
  //   Instruction [15-11]
  //   Instruction [20-16]
  //   Instruction [25-21]
endmodule

module Control (
  input  [5:0] op,
  output RegDest,
  output Branch,
  output MemRead,
  output MemWrite,
  output RegWrite,
  output ALUSrc,
  output out_8,
  output out_9,
  output out_10,
  output out_11,
  output out_12,
  output out_13,
  output [2:0] ALUOp
);

  wire [15:15] rom_1_data;

  ROM #(.addrWidth(6), .dataWidth(16)) rom_1 (
    .addr(op),
    .data({rom_1_data[15], ALUOp, out_13, out_12, out_11, out_10, out_9, out_8, ALUSrc, RegWrite, MemWrite, MemRead, Branch, RegDest}));
endmodule
