// Logisim project trab1.circ as structural Verilog: 1 circuit, main circuit main
module main (
  input  write,
  input  clk,
  output [31:0] saida
);

  wire [31:0] adder_1_out, register_1_q;

  Register #(.width(32)) register_1 (.D(adder_1_out), .en(write), .clk(clk), .Q(register_1_q), .clr(1'b0));
  Adder #(.width(32)) adder_1 (.a(register_1_q), .b(32'h4), .out(adder_1_out), .cin(1'b0));  // open: cout
  ROM #(.addrWidth(24), .dataWidth(32)) rom_1 (.addr(register_1_q[25:2]), .data(saida));
endmodule
