// Logisim project trab3.circ as structural Verilog
module main (
  input  [4:0] in_1,
  input  [4:0] in_2,
  input  [4:0] in_3,
  input  [2:0] in_4,
  input  in_5,
  input  in_6,
  output [31:0] out_7,
  output out_8
);

  wire [31:0] registers_1_out_7, registers_1_out_8;

  Registers registers_1 (
    .ReadRegister1(in_1), .ReadRegister2(in_2), .WriteRegister(in_3), .WriteData(out_7), .Write(in_5),
    .CLK(in_6), .out_7(registers_1_out_7), .out_8(registers_1_out_8));
  ALU alu_1 (.in1(registers_1_out_7), .in2(registers_1_out_8), .ALUop(in_4), .ALUout(out_7), .zero(out_8));
endmodule

module Registers (
  input  [4:0] ReadRegister1,
  input  [4:0] ReadRegister2,
  input  [4:0] WriteRegister,
  input  [31:0] WriteData,
  input  Write,
  input  CLK,
  output [31:0] out_7,
  output [31:0] out_8
);

  wire demultiplexer_1_out0, demultiplexer_1_out1, demultiplexer_1_out2, demultiplexer_1_out3,
       demultiplexer_1_out4, demultiplexer_1_out5, demultiplexer_1_out6, demultiplexer_1_out7,
       demultiplexer_1_out8, demultiplexer_1_out9, demultiplexer_1_out10, demultiplexer_1_out11,
       demultiplexer_1_out12, demultiplexer_1_out13, demultiplexer_1_out14, demultiplexer_1_out15,
       demultiplexer_1_out16, demultiplexer_1_out17, demultiplexer_1_out18, demultiplexer_1_out19,
       demultiplexer_1_out20, demultiplexer_1_out21, demultiplexer_1_out22, demultiplexer_1_out23,
       demultiplexer_1_out24, demultiplexer_1_out25, demultiplexer_1_out26, demultiplexer_1_out27,
       demultiplexer_1_out28, demultiplexer_1_out29, demultiplexer_1_out30, demultiplexer_1_out31;
  wire [31:0] register_1_q, register_2_q, register_3_q, register_4_q, register_5_q, register_6_q,
       register_7_q, register_8_q, register_9_q, register_10_q, register_11_q, register_12_q, register_13_q,
       register_14_q, register_15_q, register_16_q, register_17_q, register_18_q, register_19_q,
       register_20_q, register_21_q, register_22_q, register_23_q, register_24_q, register_25_q,
       register_26_q, register_27_q, register_28_q, register_29_q, register_30_q, register_31_q,
       register_32_q;

  Demultiplexer #(.select(5), .enable("false")) demultiplexer_1 (
    .out0(demultiplexer_1_out0), .out1(demultiplexer_1_out1), .out2(demultiplexer_1_out2),
    .out3(demultiplexer_1_out3), .out4(demultiplexer_1_out4), .out5(demultiplexer_1_out5),
    .out6(demultiplexer_1_out6), .out7(demultiplexer_1_out7), .out8(demultiplexer_1_out8),
    .out9(demultiplexer_1_out9), .out10(demultiplexer_1_out10), .out11(demultiplexer_1_out11),
    .out12(demultiplexer_1_out12), .out13(demultiplexer_1_out13), .out14(demultiplexer_1_out14),
    .out15(demultiplexer_1_out15), .out16(demultiplexer_1_out16), .out17(demultiplexer_1_out17),
    .out18(demultiplexer_1_out18), .out19(demultiplexer_1_out19), .out20(demultiplexer_1_out20),
    .out21(demultiplexer_1_out21), .out22(demultiplexer_1_out22), .out23(demultiplexer_1_out23),
    .out24(demultiplexer_1_out24), .out25(demultiplexer_1_out25), .out26(demultiplexer_1_out26),
    .out27(demultiplexer_1_out27), .out28(demultiplexer_1_out28), .out29(demultiplexer_1_out29),
    .out30(demultiplexer_1_out30), .out31(demultiplexer_1_out31), .in(Write), .sel(WriteRegister));
  Register #(.width(32)) register_1 (.D(WriteData), .en(demultiplexer_1_out0), .clk(CLK), .Q(register_1_q), .clr(1'b1));
  Register #(.width(32)) register_2 (.D(WriteData), .en(demultiplexer_1_out1), .clk(CLK), .Q(register_2_q), .clr(1'b0));
  Register #(.width(32)) register_3 (.D(WriteData), .en(demultiplexer_1_out2), .clk(CLK), .Q(register_3_q), .clr(1'b0));
  Register #(.width(32)) register_4 (.D(WriteData), .en(demultiplexer_1_out3), .clk(CLK), .Q(register_4_q), .clr(1'b0));
  Register #(.width(32)) register_5 (.D(WriteData), .en(demultiplexer_1_out4), .clk(CLK), .Q(register_5_q), .clr(1'b0));
  Register #(.width(32)) register_6 (.D(WriteData), .en(demultiplexer_1_out5), .clk(CLK), .Q(register_6_q), .clr(1'b0));
  Register #(.width(32)) register_7 (.D(WriteData), .en(demultiplexer_1_out6), .clk(CLK), .Q(register_7_q), .clr(1'b0));
  Register #(.width(32)) register_8 (.D(WriteData), .en(demultiplexer_1_out7), .clk(CLK), .Q(register_8_q), .clr(1'b0));
  Register #(.width(32)) register_9 (.D(WriteData), .en(demultiplexer_1_out8), .clk(CLK), .Q(register_9_q), .clr(1'b0));
  Register #(.width(32)) register_10 (
    .D(WriteData), .en(demultiplexer_1_out9), .clk(CLK), .Q(register_10_q), .clr(1'b0));
  Register #(.width(32)) register_11 (
    .D(WriteData), .en(demultiplexer_1_out10), .clk(CLK), .Q(register_11_q), .clr(1'b0));
  Register #(.width(32)) register_12 (
    .D(WriteData), .en(demultiplexer_1_out11), .clk(CLK), .Q(register_12_q), .clr(1'b0));
  Register #(.width(32)) register_13 (
    .D(WriteData), .en(demultiplexer_1_out12), .clk(CLK), .Q(register_13_q), .clr(1'b0));
  Register #(.width(32)) register_14 (
    .D(WriteData), .en(demultiplexer_1_out13), .clk(CLK), .Q(register_14_q), .clr(1'b0));
  Register #(.width(32)) register_15 (
    .D(WriteData), .en(demultiplexer_1_out14), .clk(CLK), .Q(register_15_q), .clr(1'b0));
  Register #(.width(32)) register_16 (
    .D(WriteData), .en(demultiplexer_1_out15), .clk(CLK), .Q(register_16_q), .clr(1'b0));
  Register #(.width(32)) register_17 (
    .D(WriteData), .en(demultiplexer_1_out16), .clk(CLK), .Q(register_17_q), .clr(1'b0));
  Register #(.width(32)) register_18 (
    .D(WriteData), .en(demultiplexer_1_out17), .clk(CLK), .Q(register_18_q), .clr(1'b0));
  Register #(.width(32)) register_19 (
    .D(WriteData), .en(demultiplexer_1_out18), .clk(CLK), .Q(register_19_q), .clr(1'b0));
  Register #(.width(32)) register_20 (
    .D(WriteData), .en(demultiplexer_1_out19), .clk(CLK), .Q(register_20_q), .clr(1'b0));
  Register #(.width(32)) register_21 (
    .D(WriteData), .en(demultiplexer_1_out20), .clk(CLK), .Q(register_21_q), .clr(1'b0));
  Register #(.width(32)) register_22 (
    .D(WriteData), .en(demultiplexer_1_out21), .clk(CLK), .Q(register_22_q), .clr(1'b0));
  Register #(.width(32)) register_23 (
    .D(WriteData), .en(demultiplexer_1_out22), .clk(CLK), .Q(register_23_q), .clr(1'b0));
  Register #(.width(32)) register_24 (
    .D(WriteData), .en(demultiplexer_1_out23), .clk(CLK), .Q(register_24_q), .clr(1'b0));
  Register #(.width(32)) register_25 (
    .D(WriteData), .en(demultiplexer_1_out24), .clk(CLK), .Q(register_25_q), .clr(1'b0));
  Register #(.width(32)) register_26 (
    .D(WriteData), .en(demultiplexer_1_out25), .clk(CLK), .Q(register_26_q), .clr(1'b0));
  Register #(.width(32)) register_27 (
    .D(WriteData), .en(demultiplexer_1_out26), .clk(CLK), .Q(register_27_q), .clr(1'b0));
  Register #(.width(32)) register_28 (
    .D(WriteData), .en(demultiplexer_1_out27), .clk(CLK), .Q(register_28_q), .clr(1'b0));
  Register #(.width(32)) register_29 (
    .D(WriteData), .en(demultiplexer_1_out28), .clk(CLK), .Q(register_29_q), .clr(1'b0));
  Register #(.width(32)) register_30 (
    .D(WriteData), .en(demultiplexer_1_out29), .clk(CLK), .Q(register_30_q), .clr(1'b0));
  Register #(.width(32)) register_31 (
    .D(WriteData), .en(demultiplexer_1_out30), .clk(CLK), .Q(register_31_q), .clr(1'b0));
  Register #(.width(32)) register_32 (
    .D(WriteData), .en(demultiplexer_1_out31), .clk(CLK), .Q(register_32_q), .clr(1'b0));
  Multiplexer #(.select(5), .width(32), .enable("false")) multiplexer_1 (
    .in0(register_1_q), .in1(register_2_q), .in2(register_3_q), .in3(register_4_q), .in4(register_5_q),
    .in5(register_6_q), .in6(register_7_q), .in7(register_8_q), .in8(register_9_q), .in9(register_10_q),
    .in10(register_11_q), .in11(register_12_q), .in12(register_13_q), .in13(register_14_q),
    .in14(register_15_q), .in15(register_16_q), .in16(register_17_q), .in17(register_18_q),
    .in18(register_19_q), .in19(register_20_q), .in20(register_21_q), .in21(register_22_q),
    .in22(register_23_q), .in23(register_24_q), .in24(register_25_q), .in25(register_26_q),
    .in26(register_27_q), .in27(register_28_q), .in28(register_29_q), .in29(register_30_q),
    .in30(register_31_q), .in31(register_32_q), .out(out_7), .sel(ReadRegister1));
  Multiplexer #(.select(5), .width(32), .enable("false")) multiplexer_2 (
    .in0(register_1_q), .in1(register_2_q), .in2(register_3_q), .in3(register_4_q), .in4(register_5_q),
    .in5(register_6_q), .in6(register_7_q), .in7(register_8_q), .in8(register_9_q), .in9(register_10_q),
    .in10(register_11_q), .in11(register_12_q), .in12(register_13_q), .in13(register_14_q),
    .in14(register_15_q), .in15(register_16_q), .in16(register_17_q), .in17(register_18_q),
    .in18(register_19_q), .in19(register_20_q), .in20(register_21_q), .in21(register_22_q),
    .in22(register_23_q), .in23(register_24_q), .in24(register_25_q), .in25(register_26_q),
    .in26(register_27_q), .in27(register_28_q), .in28(register_29_q), .in29(register_30_q),
    .in30(register_31_q), .in31(register_32_q), .out(out_8), .sel(ReadRegister2));
endmodule

module ALU (
  input  [31:0] in1,
  input  [31:0] in2,
  input  [2:0] ALUop,
  output [31:0] ALUout,
  output zero
);

  wire or_2_out;
  wire [31:0] adder_1_out, and_1_out, nor_1_out, or_1_out, subtractor_1_out;

  Adder #(.width(32)) adder_1 (.a(in1), .b(in2), .out(adder_1_out), .cin(1'b0));  // open: cout
  Subtractor #(.width(32)) subtractor_1 (.a(in1), .b(in2), .out(subtractor_1_out), .bin(1'b0));  // open: bout
  assign and_1_out = in1 & in2;  // AND_Gate and_1, 32 bits wide
  assign or_1_out = in1 | in2;  // OR_Gate or_1, 32 bits wide
  assign nor_1_out = ~(in1 | in2);  // NOR_Gate nor_1, 32 bits wide
  Multiplexer #(.select(3), .width(32), .enable("false")) multiplexer_1 (
    .in0(adder_1_out), .in1(subtractor_1_out), .in2(and_1_out), .in3(or_1_out), .in4(nor_1_out),
    .out(ALUout), .sel(ALUop));  // open: in5, in6, in7
  or or_2 (or_2_out, ALUout[0], ALUout[1], ALUout[2], ALUout[3], ALUout[4], ALUout[5], ALUout[6], ALUout[7], ALUout[8], ALUout[9], ALUout[10], ALUout[11], ALUout[12], ALUout[13], ALUout[14], ALUout[15], ALUout[17], ALUout[18], ALUout[19], ALUout[20], ALUout[21], ALUout[22], ALUout[23], ALUout[24], ALUout[25], ALUout[26], ALUout[27], ALUout[28], ALUout[29], ALUout[30], ALUout[31], ALUout[16]);
  not not_1 (zero, or_2_out);
endmodule

module Memory (
  input  [31:0] Address,
  input  [31:0] Data,
  input  CLK,
  input  Write,
  input  Read,
  input  [1:0] whb
);

  wire undriven;
  wire [1:0] demultiplexer_4_out0, demultiplexer_4_out1;
  wire [3:0] demultiplexer_1_out0, multiplexer_2_out;
  wire [7:0] demultiplexer_3_out0, demultiplexer_3_out1, demultiplexer_3_out2, demultiplexer_3_out3,
       multiplexer_4_out, ram_1_dout, ram_2_dout, ram_3_dout, ram_4_dout;
  wire [15:0] demultiplexer_2_out0, demultiplexer_2_out1, multiplexer_3_out;
  wire [31:0] multiplexer_1_out;

  Demultiplexer #(.select(2), .enable("false")) demultiplexer_1 (
    .out0(demultiplexer_1_out0[0]), .out1(demultiplexer_1_out0[1]), .out2(demultiplexer_1_out0[2]),
    .out3(demultiplexer_1_out0[3]), .in(Write), .sel(Address[1:0]));
  Demultiplexer #(.width(16), .enable("false")) demultiplexer_2 (
    .out0(demultiplexer_2_out0), .out1(demultiplexer_2_out1), .in(Data[15:0]), .sel(Address[1]));
  Demultiplexer #(.select(2), .width(8), .enable("false")) demultiplexer_3 (
    .out0(demultiplexer_3_out0), .out1(demultiplexer_3_out1), .out2(demultiplexer_3_out2),
    .out3(demultiplexer_3_out3), .in(Data[7:0]), .sel(Address[1:0]));
  Demultiplexer #(.width(2), .enable("false")) demultiplexer_4 (
    .out0(demultiplexer_4_out0), .out1(demultiplexer_4_out1), .in({2{Write}}), .sel(Address[1]));
  Multiplexer #(.select(2), .width(32), .enable("false")) multiplexer_1 (
    .in0(Data), .in1({demultiplexer_2_out1, demultiplexer_2_out0}),
    .in2({demultiplexer_3_out3, demultiplexer_3_out2, demultiplexer_3_out1, demultiplexer_3_out0}),
    .out(multiplexer_1_out), .sel(whb));  // open: in3
  Multiplexer #(.select(2), .width(4), .enable("false")) multiplexer_2 (
    .in0({4{Write}}), .in1({demultiplexer_4_out1, demultiplexer_4_out0}), .in2(demultiplexer_1_out0),
    .out(multiplexer_2_out), .sel(whb));  // open: in3
  RAM #(.addrWidth(24), .databus("bibus")) ram_1 (
    .addr(Address[25:2]), .we(multiplexer_2_out[0]), .oe(Read), .clk(undriven), .din(multiplexer_1_out[7:0]),
    .dout(ram_1_dout));
  RAM #(.addrWidth(24), .databus("bibus")) ram_2 (
    .addr(Address[25:2]), .we(multiplexer_2_out[1]), .oe(Read), .clk(undriven),
    .din(multiplexer_1_out[15:8]), .dout(ram_2_dout));
  RAM #(.addrWidth(24), .databus("bibus")) ram_3 (
    .addr(Address[25:2]), .we(multiplexer_2_out[2]), .oe(Read), .clk(undriven),
    .din(multiplexer_1_out[23:16]), .dout(ram_3_dout));
  RAM #(.addrWidth(24), .databus("bibus")) ram_4 (
    .addr(Address[25:2]), .we(multiplexer_2_out[3]), .oe(Read), .clk(undriven),
    .din(multiplexer_1_out[31:24]), .dout(ram_4_dout));
  Multiplexer #(.width(16), .enable("false")) multiplexer_3 (
    .in0({ram_2_dout, ram_1_dout}), .in1({ram_4_dout, ram_3_dout}), .out(multiplexer_3_out));  // open: sel
  Multiplexer #(.select(2), .width(8), .enable("false")) multiplexer_4 (
    .in0(ram_1_dout), .in1(ram_2_dout), .in2(ram_3_dout), .in3(ram_4_dout), .out(multiplexer_4_out));  // open: sel
  Multiplexer #(.select(2), .width(32), .enable("false")) multiplexer_5 (
    .in0({ram_4_dout, ram_3_dout, ram_2_dout, ram_1_dout}), .in1({{16{1'b0}}, multiplexer_3_out}),
    .in2({{24{1'b0}}, multiplexer_4_out}));  // open: in3, out, sel
endmodule

module c1 (
  input  write,
  input  clk,
  output [31:0] saida
);

  wire [31:0] adder_1_out, register_1_q;

  Register #(.width(32)) register_1 (.D(adder_1_out), .en(write), .clk(clk), .Q(register_1_q), .clr(1'b0));
  Adder #(.width(32)) adder_1 (.a(register_1_q), .b(32'h4), .out(adder_1_out), .cin(1'b0));  // open: cout
  ROM #(.addrWidth(24), .dataWidth(32)) rom_1 (.addr(register_1_q[25:2]), .data(saida));
endmodule

module singExt (
  input  [15:0] signextIN,
  input  [31:0] signextOUT
);


  assign signextOUT = {{17{signextIN[15]}}, signextIN[14:0]};
endmodule
