// Logisim project trab5.circ as structural Verilog: 14 circuits, main circuit main
module main (
  input  CLEAR
);

  wire alu_1_zero, alucontrol_1_jumpregister, and_1_out, clock_1_out, control_1_alusrc, control_1_branch,
       control_1_j, control_1_memread, control_1_memwrite, control_1_regwrite;
  wire [1:0] control_1_memtoreg, control_1_regdst, control_1_whb;
  wire [2:0] alucontrol_1_alucontrolout, control_1_aluop;
  wire [3:0] pcsplitter_1_pc31_28;
  wire [4:0] instructionsplitter_1_instruction15_11, instructionsplitter_1_instruction20_16,
       instructionsplitter_1_instruction25_21, multiplexer_2_out;
  wire [5:0] instructionsplitter_1_instruction5_0, instructionsplitter_1_instruction31_26;
  wire [6:0] bit_extender_2_out;
  wire [15:0] instructionsplitter_1_instruction15_0;
  wire [25:0] instructionsplitter_1_instruction25_0;
  wire [31:0] adder_1_out, adder_2_out, alu_1_aluresult, bit_extender_1_out, instructionmemory_1_instruction,
       joiner_1_jump31_0, memory_1_readdata, multiplexer_1_out, multiplexer_3_out, multiplexer_4_out,
       multiplexer_5_out, multiplexer_6_out, pc_1_q, registers_1_readdata1, registers_1_readdata2,
       shiftleft2_1_shiftleft2out, shiftleft2_2_shiftleft2out, signextend_1_signextendout;

  Clock clock_1 (.out(clock_1_out));
  PC pc_1 (.D(multiplexer_1_out), .WriteEnable(1'b1), .CLK(clock_1_out), .Q(pc_1_q));
  // Probe on instructionmemory_1_instruction
  InstructionMemory instructionmemory_1 (.ReadAddress(pc_1_q), .Instruction(instructionmemory_1_instruction));
  Adder #(.width(32)) adder_1 (.a(pc_1_q), .b(32'h4), .out(adder_1_out), .cin(1'b0));  // open: cout
  PCSplitter pcsplitter_1 (.PCIn(adder_1_out), .PC31_28(pcsplitter_1_pc31_28));
  InstructionSplitter instructionsplitter_1 (
    .InstructionSplitterIn(instructionmemory_1_instruction),
    .Instruction31_26(instructionsplitter_1_instruction31_26),
    .Instruction25_21(instructionsplitter_1_instruction25_21),
    .Instruction20_16(instructionsplitter_1_instruction20_16),
    .Instruction15_11(instructionsplitter_1_instruction15_11),
    .Instruction15_0(instructionsplitter_1_instruction15_0),
    .Instruction5_0(instructionsplitter_1_instruction5_0),
    .Instruction25_0(instructionsplitter_1_instruction25_0));
  Multiplexer #(.width(32), .enable("false")) multiplexer_1 (
    .in0(multiplexer_3_out), .in1(registers_1_readdata1), .out(multiplexer_1_out),
    .sel(alucontrol_1_jumpregister));
  assign bit_extender_1_out = {{6{1'b0}}, instructionsplitter_1_instruction25_0};  // Bit_Extender bit_extender_1
  Multiplexer #(.select(2), .width(5), .enable("false")) multiplexer_2 (
    .in0(instructionsplitter_1_instruction20_16), .in1(instructionsplitter_1_instruction15_11),
    .in2({5{1'b1}}), .out(multiplexer_2_out), .sel(control_1_regdst));  // open: in3
  ShiftLeft2 shiftleft2_1 (.ShiftLeft2In(bit_extender_1_out), .ShiftLeft2Out(shiftleft2_1_shiftleft2out));
  Control control_1 (
    .Instruction31_26(instructionsplitter_1_instruction31_26), .RegDst(control_1_regdst),
    .Branch(control_1_branch), .MemRead(control_1_memread), .MemtoReg(control_1_memtoreg),
    .MemWrite(control_1_memwrite), .ALUSrc(control_1_alusrc), .RegWrite(control_1_regwrite),
    .whb(control_1_whb), .j(control_1_j), .ALUOp(control_1_aluop));
  Multiplexer #(.width(32), .enable("false")) multiplexer_3 (
    .in0(multiplexer_5_out), .in1(joiner_1_jump31_0), .out(multiplexer_3_out), .sel(control_1_j));
  Joiner joiner_1 (.Jump27_0(shiftleft2_1_shiftleft2out), .PC31_28(pcsplitter_1_pc31_28), .Jump31_0(joiner_1_jump31_0));
  Registers registers_1 (
    .ReadRegister1(instructionsplitter_1_instruction25_21),
    .ReadRegister2(instructionsplitter_1_instruction20_16), .WriteRegister(multiplexer_2_out),
    .WriteData(multiplexer_6_out), .RegWrite(control_1_regwrite), .CLK(clock_1_out),
    .ReadData1(registers_1_readdata1), .ReadData2(registers_1_readdata2));
  SignExtend signextend_1 (
    .SignExtendIn(instructionsplitter_1_instruction15_0), .SignExtendOut(signextend_1_signextendout));
  ALUControl alucontrol_1 (
    .Instruction5_0(instructionsplitter_1_instruction5_0), .ALUOp(control_1_aluop),
    .ALUControlOut(alucontrol_1_alucontrolout), .JumpRegister(alucontrol_1_jumpregister));
  Multiplexer #(.width(32), .enable("false")) multiplexer_4 (
    .in0(registers_1_readdata2), .in1(signextend_1_signextendout), .out(multiplexer_4_out),
    .sel(control_1_alusrc));
  TTY tty_1 (.data(bit_extender_2_out), .clk(clock_1_out), .clr(CLEAR));  // open: we
  ShiftLeft2 shiftleft2_2 (.ShiftLeft2In(signextend_1_signextendout), .ShiftLeft2Out(shiftleft2_2_shiftleft2out));
  ALU alu_1 (
    .in1(registers_1_readdata1), .in2(multiplexer_4_out), .ALUop(alucontrol_1_alucontrolout),
    .ALUResult(alu_1_aluresult), .Zero(alu_1_zero));
  Adder #(.width(32)) adder_2 (
    .a(adder_1_out), .b(shiftleft2_2_shiftleft2out), .out(adder_2_out), .cin(1'b0));  // open: cout
  and and_1 (and_1_out, control_1_branch, alu_1_zero);
  Bit_Extender #(.in_width(32), .out_width(7), .\type ("zero")) bit_extender_2 (
    .in(alu_1_aluresult), .out(bit_extender_2_out));
  Multiplexer #(.width(32), .enable("false")) multiplexer_5 (
    .in0(adder_1_out), .in1(adder_2_out), .out(multiplexer_5_out), .sel(and_1_out));
  Memory memory_1 (
    .Address(alu_1_aluresult), .Data(registers_1_readdata2), .Write(control_1_memwrite),
    .Read(control_1_memread), .whb(control_1_whb), .CLK(clock_1_out), .ReadData(memory_1_readdata));
  // Probe on memory_1_readdata
  Multiplexer #(.select(2), .width(32), .enable("false")) multiplexer_6 (
    .in0(alu_1_aluresult), .in1(memory_1_readdata), .in2(adder_1_out), .out(multiplexer_6_out),
    .sel(control_1_memtoreg));  // open: in3

  // Notes on the sheet:
  //   JumpRegister
  //   RegDst
  //   ALUSrc
  //   Branch
  //   PCSrc
  //   MemtoReg
endmodule

module Registers (
  input  [4:0] ReadRegister1,
  input  [4:0] ReadRegister2,
  input  [4:0] WriteRegister,
  input  [31:0] WriteData,
  input  RegWrite,
  input  CLK,
  output [31:0] ReadData1,
  output [31:0] ReadData2
);

  wire demultiplexer_1_out0, demultiplexer_1_out1, demultiplexer_1_out2, demultiplexer_1_out3,
       demultiplexer_1_out4, demultiplexer_1_out5, demultiplexer_1_out6, demultiplexer_1_out7,
       demultiplexer_1_out8, demultiplexer_1_out9, demultiplexer_1_out10, demultiplexer_1_out11,
       demultiplexer_1_out12, demultiplexer_1_out13, demultiplexer_1_out14, demultiplexer_1_out15,
       demultiplexer_1_out16, demultiplexer_1_out17, demultiplexer_1_out18, demultiplexer_1_out19,
       demultiplexer_1_out20, demultiplexer_1_out21, demultiplexer_1_out22, demultiplexer_1_out23,
       demultiplexer_1_out24, demultiplexer_1_out25, demultiplexer_1_out26, demultiplexer_1_out27,
       demultiplexer_1_out28, demultiplexer_1_out29, demultiplexer_1_out30, demultiplexer_1_out31;
  wire [31:0] register_1_q, register_2_q, register_3_q, register_4_q, register_5_q, register_6_q,
       register_7_q, register_8_q, register_9_q, register_10_q, register_11_q, register_12_q, register_13_q,
       register_14_q, register_15_q, register_16_q, register_17_q, register_18_q, register_19_q,
       register_20_q, register_21_q, register_22_q, register_23_q, register_24_q, register_25_q,
       register_26_q, register_27_q, register_28_q, register_29_q, register_30_q, register_31_q,
       register_32_q;

  Demultiplexer #(.select(5), .enable("false")) demultiplexer_1 (
    .out0(demultiplexer_1_out0), .out1(demultiplexer_1_out1), .out2(demultiplexer_1_out2),
    .out3(demultiplexer_1_out3), .out4(demultiplexer_1_out4), .out5(demultiplexer_1_out5),
    .out6(demultiplexer_1_out6), .out7(demultiplexer_1_out7), .out8(demultiplexer_1_out8),
    .out9(demultiplexer_1_out9), .out10(demultiplexer_1_out10), .out11(demultiplexer_1_out11),
    .out12(demultiplexer_1_out12), .out13(demultiplexer_1_out13), .out14(demultiplexer_1_out14),
    .out15(demultiplexer_1_out15), .out16(demultiplexer_1_out16), .out17(demultiplexer_1_out17),
    .out18(demultiplexer_1_out18), .out19(demultiplexer_1_out19), .out20(demultiplexer_1_out20),
    .out21(demultiplexer_1_out21), .out22(demultiplexer_1_out22), .out23(demultiplexer_1_out23),
    .out24(demultiplexer_1_out24), .out25(demultiplexer_1_out25), .out26(demultiplexer_1_out26),
    .out27(demultiplexer_1_out27), .out28(demultiplexer_1_out28), .out29(demultiplexer_1_out29),
    .out30(demultiplexer_1_out30), .out31(demultiplexer_1_out31), .in(RegWrite), .sel(WriteRegister));
  Register #(.width(32)) register_1 (.D(WriteData), .en(demultiplexer_1_out0), .clk(CLK), .Q(register_1_q), .clr(1'b1));
  Register #(.width(32)) register_2 (.D(WriteData), .en(demultiplexer_1_out1), .clk(CLK), .Q(register_2_q), .clr(1'b0));
  Register #(.width(32)) register_3 (.D(WriteData), .en(demultiplexer_1_out2), .clk(CLK), .Q(register_3_q), .clr(1'b0));
  Register #(.width(32)) register_4 (.D(WriteData), .en(demultiplexer_1_out3), .clk(CLK), .Q(register_4_q), .clr(1'b0));
  Register #(.width(32)) register_5 (.D(WriteData), .en(demultiplexer_1_out4), .clk(CLK), .Q(register_5_q), .clr(1'b0));
  Register #(.width(32)) register_6 (.D(WriteData), .en(demultiplexer_1_out5), .clk(CLK), .Q(register_6_q), .clr(1'b0));
  Register #(.width(32)) register_7 (.D(WriteData), .en(demultiplexer_1_out6), .clk(CLK), .Q(register_7_q), .clr(1'b0));
  Register #(.width(32)) register_8 (.D(WriteData), .en(demultiplexer_1_out7), .clk(CLK), .Q(register_8_q), .clr(1'b0));
  Register #(.width(32)) register_9 (.D(WriteData), .en(demultiplexer_1_out8), .clk(CLK), .Q(register_9_q), .clr(1'b0));
  Register #(.width(32)) register_10 (
    .D(WriteData), .en(demultiplexer_1_out9), .clk(CLK), .Q(register_10_q), .clr(1'b0));
  Register #(.width(32)) register_11 (
    .D(WriteData), .en(demultiplexer_1_out10), .clk(CLK), .Q(register_11_q), .clr(1'b0));
  Register #(.width(32)) register_12 (
    .D(WriteData), .en(demultiplexer_1_out11), .clk(CLK), .Q(register_12_q), .clr(1'b0));
  Register #(.width(32)) register_13 (
    .D(WriteData), .en(demultiplexer_1_out12), .clk(CLK), .Q(register_13_q), .clr(1'b0));
  Register #(.width(32)) register_14 (
    .D(WriteData), .en(demultiplexer_1_out13), .clk(CLK), .Q(register_14_q), .clr(1'b0));
  Register #(.width(32)) register_15 (
    .D(WriteData), .en(demultiplexer_1_out14), .clk(CLK), .Q(register_15_q), .clr(1'b0));
  Register #(.width(32)) register_16 (
    .D(WriteData), .en(demultiplexer_1_out15), .clk(CLK), .Q(register_16_q), .clr(1'b0));
  Register #(.width(32)) register_17 (
    .D(WriteData), .en(demultiplexer_1_out16), .clk(CLK), .Q(register_17_q), .clr(1'b0));
  Register #(.width(32)) register_18 (
    .D(WriteData), .en(demultiplexer_1_out17), .clk(CLK), .Q(register_18_q), .clr(1'b0));
  Register #(.width(32)) register_19 (
    .D(WriteData), .en(demultiplexer_1_out18), .clk(CLK), .Q(register_19_q), .clr(1'b0));
  Register #(.width(32)) register_20 (
    .D(WriteData), .en(demultiplexer_1_out19), .clk(CLK), .Q(register_20_q), .clr(1'b0));
  Register #(.width(32)) register_21 (
    .D(WriteData), .en(demultiplexer_1_out20), .clk(CLK), .Q(register_21_q), .clr(1'b0));
  Register #(.width(32)) register_22 (
    .D(WriteData), .en(demultiplexer_1_out21), .clk(CLK), .Q(register_22_q), .clr(1'b0));
  Register #(.width(32)) register_23 (
    .D(WriteData), .en(demultiplexer_1_out22), .clk(CLK), .Q(register_23_q), .clr(1'b0));
  Register #(.width(32)) register_24 (
    .D(WriteData), .en(demultiplexer_1_out23), .clk(CLK), .Q(register_24_q), .clr(1'b0));
  Register #(.width(32)) register_25 (
    .D(WriteData), .en(demultiplexer_1_out24), .clk(CLK), .Q(register_25_q), .clr(1'b0));
  Register #(.width(32)) register_26 (
    .D(WriteData), .en(demultiplexer_1_out25), .clk(CLK), .Q(register_26_q), .clr(1'b0));
  Register #(.width(32)) register_27 (
    .D(WriteData), .en(demultiplexer_1_out26), .clk(CLK), .Q(register_27_q), .clr(1'b0));
  Register #(.width(32)) register_28 (
    .D(WriteData), .en(demultiplexer_1_out27), .clk(CLK), .Q(register_28_q), .clr(1'b0));
  Register #(.width(32)) register_29 (
    .D(WriteData), .en(demultiplexer_1_out28), .clk(CLK), .Q(register_29_q), .clr(1'b0));
  Register #(.width(32)) register_30 (
    .D(WriteData), .en(demultiplexer_1_out29), .clk(CLK), .Q(register_30_q), .clr(1'b0));
  Register #(.width(32)) register_31 (
    .D(WriteData), .en(demultiplexer_1_out30), .clk(CLK), .Q(register_31_q), .clr(1'b0));
  Register #(.width(32)) register_32 (
    .D(WriteData), .en(demultiplexer_1_out31), .clk(CLK), .Q(register_32_q), .clr(1'b0));
  Multiplexer #(.select(5), .width(32), .enable("false")) multiplexer_1 (
    .in0(register_1_q), .in1(register_2_q), .in2(register_3_q), .in3(register_4_q), .in4(register_5_q),
    .in5(register_6_q), .in6(register_7_q), .in7(register_8_q), .in8(register_9_q), .in9(register_10_q),
    .in10(register_11_q), .in11(register_12_q), .in12(register_13_q), .in13(register_14_q),
    .in14(register_15_q), .in15(register_16_q), .in16(register_17_q), .in17(register_18_q),
    .in18(register_19_q), .in19(register_20_q), .in20(register_21_q), .in21(register_22_q),
    .in22(register_23_q), .in23(register_24_q), .in24(register_25_q), .in25(register_26_q),
    .in26(register_27_q), .in27(register_28_q), .in28(register_29_q), .in29(register_30_q),
    .in30(register_31_q), .in31(register_32_q), .out(ReadData1), .sel(ReadRegister1));
  Multiplexer #(.select(5), .width(32), .enable("false")) multiplexer_2 (
    .in0(register_1_q), .in1(register_2_q), .in2(register_3_q), .in3(register_4_q), .in4(register_5_q),
    .in5(register_6_q), .in6(register_7_q), .in7(register_8_q), .in8(register_9_q), .in9(register_10_q),
    .in10(register_11_q), .in11(register_12_q), .in12(register_13_q), .in13(register_14_q),
    .in14(register_15_q), .in15(register_16_q), .in16(register_17_q), .in17(register_18_q),
    .in18(register_19_q), .in19(register_20_q), .in20(register_21_q), .in21(register_22_q),
    .in22(register_23_q), .in23(register_24_q), .in24(register_25_q), .in25(register_26_q),
    .in26(register_27_q), .in27(register_28_q), .in28(register_29_q), .in29(register_30_q),
    .in30(register_31_q), .in31(register_32_q), .out(ReadData2), .sel(ReadRegister2));
endmodule

module ALU (
  input  [31:0] in1,
  input  [31:0] in2,
  input  [2:0] ALUop,
  output [31:0] ALUResult,
  output Zero
);

  wire or_2_out;
  wire [31:0] adder_1_out, and_1_out, nor_1_out, or_1_out, subtractor_1_out;

  Adder #(.width(32)) adder_1 (.a(in1), .b(in2), .out(adder_1_out), .cin(1'b0));  // open: cout
  Subtractor #(.width(32)) subtractor_1 (.a(in1), .b(in2), .out(subtractor_1_out), .bin(1'b0));  // open: bout
  assign and_1_out = in1 & in2;  // AND_Gate and_1, 32 bits wide
  assign or_1_out = in1 | in2;  // OR_Gate or_1, 32 bits wide
  assign nor_1_out = ~(in1 | in2);  // NOR_Gate nor_1, 32 bits wide
  Multiplexer #(.select(3), .width(32), .enable("false")) multiplexer_1 (
    .in0(adder_1_out), .in1(adder_1_out), .in2(subtractor_1_out), .in3(subtractor_1_out), .in4(and_1_out),
    .in5(or_1_out), .in6({32{1'b0}}), .in7(nor_1_out), .out(ALUResult), .sel(ALUop));
  or or_2 (or_2_out, ALUResult[0], ALUResult[1], ALUResult[2], ALUResult[3], ALUResult[4], ALUResult[5], ALUResult[6], ALUResult[7], ALUResult[8], ALUResult[9], ALUResult[10], ALUResult[11], ALUResult[12], ALUResult[13], ALUResult[14], ALUResult[15], ALUResult[17], ALUResult[18], ALUResult[19], ALUResult[20], ALUResult[21], ALUResult[22], ALUResult[23], ALUResult[24], ALUResult[25], ALUResult[26], ALUResult[27], ALUResult[28], ALUResult[29], ALUResult[30], ALUResult[31], ALUResult[16]);
  not not_1 (Zero, or_2_out);
endmodule

module Memory (
  input  [31:0] Address,
  input  [31:0] Data,
  input  Write,
  input  Read,
  input  [1:0] whb,
  input  CLK,
  output [31:0] ReadData
);

  wire [1:0] demultiplexer_4_out0, demultiplexer_4_out1;
  wire [3:0] demultiplexer_1_out0, multiplexer_2_out;
  wire [7:0] demultiplexer_3_out0, demultiplexer_3_out1, demultiplexer_3_out2, demultiplexer_3_out3,
       multiplexer_4_out, ram_1_dout, ram_2_dout, ram_3_dout, ram_4_dout;
  wire [15:0] demultiplexer_2_out0, demultiplexer_2_out1, multiplexer_3_out;
  wire [31:0] multiplexer_1_out;

  Demultiplexer #(.select(2), .enable("false")) demultiplexer_1 (
    .out0(demultiplexer_1_out0[0]), .out1(demultiplexer_1_out0[1]), .out2(demultiplexer_1_out0[2]),
    .out3(demultiplexer_1_out0[3]), .in(Write), .sel(Address[1:0]));
  Demultiplexer #(.width(16), .enable("false")) demultiplexer_2 (
    .out0(demultiplexer_2_out0), .out1(demultiplexer_2_out1), .in(Data[15:0]), .sel(Address[1]));
  Demultiplexer #(.select(2), .width(8), .enable("false")) demultiplexer_3 (
    .out0(demultiplexer_3_out0), .out1(demultiplexer_3_out1), .out2(demultiplexer_3_out2),
    .out3(demultiplexer_3_out3), .in(Data[7:0]), .sel(Address[1:0]));
  Demultiplexer #(.width(2), .enable("false")) demultiplexer_4 (
    .out0(demultiplexer_4_out0), .out1(demultiplexer_4_out1), .in({2{Write}}), .sel(Address[1]));
  Multiplexer #(.select(2), .width(32), .enable("false")) multiplexer_1 (
    .in0(Data), .in1({demultiplexer_2_out1, demultiplexer_2_out0}),
    .in2({demultiplexer_3_out3, demultiplexer_3_out2, demultiplexer_3_out1, demultiplexer_3_out0}),
    .in3({32{1'b0}}), .out(multiplexer_1_out), .sel(whb));
  Multiplexer #(.select(2), .width(4), .enable("false")) multiplexer_2 (
    .in0({4{Write}}), .in1({demultiplexer_4_out1, demultiplexer_4_out0}), .in2(demultiplexer_1_out0),
    .in3(4'b0000), .out(multiplexer_2_out), .sel(whb));
  RAM #(.addrWidth(24), .trigger("falling"), .databus("bibus")) ram_1 (
    .addr(Address[25:2]), .we(multiplexer_2_out[0]), .oe(Read), .clk(CLK), .din(multiplexer_1_out[7:0]),
    .dout(ram_1_dout));
  RAM #(.addrWidth(24), .trigger("falling"), .databus("bibus")) ram_2 (
    .addr(Address[25:2]), .we(multiplexer_2_out[1]), .oe(Read), .clk(CLK), .din(multiplexer_1_out[15:8]),
    .dout(ram_2_dout));
  RAM #(.addrWidth(24), .trigger("falling"), .databus("bibus")) ram_3 (
    .addr(Address[25:2]), .we(multiplexer_2_out[2]), .oe(Read), .clk(CLK), .din(multiplexer_1_out[23:16]),
    .dout(ram_3_dout));
  RAM #(.addrWidth(24), .trigger("falling"), .databus("bibus")) ram_4 (
    .addr(Address[25:2]), .we(multiplexer_2_out[3]), .oe(Read), .clk(CLK), .din(multiplexer_1_out[31:24]),
    .dout(ram_4_dout));
  Multiplexer #(.width(16), .enable("false")) multiplexer_3 (
    .in0({ram_2_dout, ram_1_dout}), .in1({ram_4_dout, ram_3_dout}), .out(multiplexer_3_out), .sel(Address[1]));
  Multiplexer #(.select(2), .width(8), .enable("false")) multiplexer_4 (
    .in0(ram_1_dout), .in1(ram_2_dout), .in2(ram_3_dout), .in3(ram_4_dout), .out(multiplexer_4_out),
    .sel(Address[1:0]));
  Multiplexer #(.select(2), .width(32), .enable("false")) multiplexer_5 (
    .in0({ram_4_dout, ram_3_dout, ram_2_dout, ram_1_dout}), .in1({{16{1'b0}}, multiplexer_3_out}),
    .in2({{24{1'b0}}, multiplexer_4_out}), .in3({32{1'b0}}), .out(ReadData), .sel(whb));

  // Notes on the sheet:
  //   a0, a1
  //   a1
  //   a0, a1
  //   a1
  //   whb
  //   a1
  //   a0, a1
  //   whb
endmodule

module SignExtend (
  input  [15:0] SignExtendIn,
  output [31:0] SignExtendOut
);


  assign SignExtendOut = {{17{SignExtendIn[15]}}, SignExtendIn[14:0]};
endmodule

module ShiftLeft2 (
  input  [31:0] ShiftLeft2In,
  output [31:0] ShiftLeft2Out
);


  assign ShiftLeft2Out = {ShiftLeft2In[29:0], 2'b00};
endmodule

module PC (
  input  [31:0] D,
  input  WriteEnable,
  input  CLK,
  output [31:0] Q
);

  Register #(.width(32)) register_1 (.D(D), .en(WriteEnable), .clk(CLK), .Q(Q), .clr(1'b0));
endmodule

module InstructionMemory (
  input  [31:0] ReadAddress,
  output [31:0] Instruction
);

  ROM #(.addrWidth(24), .dataWidth(32)) rom_1 (.addr(ReadAddress[25:2]), .data(Instruction));

  // Notes on the sheet:
  //   contents of rom_1 (hex, n*v repeats v):
  //   20010001 20020002 ac010000 ac020005 8c030000 8c040005
endmodule

module InstructionSplitter (
  input  [31:0] InstructionSplitterIn,
  output [5:0] Instruction31_26,
  output [4:0] Instruction25_21,
  output [4:0] Instruction20_16,
  output [4:0] Instruction15_11,
  output [15:0] Instruction15_0,
  output [5:0] Instruction5_0,
  output [25:0] Instruction25_0
);

  Bit_Extender #(.in_width(32), .out_width(26), .\type ("zero")) bit_extender_1 (
    .in(InstructionSplitterIn), .out(Instruction25_0));

  assign Instruction5_0 = InstructionSplitterIn[5:0];
  assign Instruction15_0 = InstructionSplitterIn[15:0];
  assign Instruction15_11 = InstructionSplitterIn[15:11];
  assign Instruction20_16 = InstructionSplitterIn[20:16];
  assign Instruction25_21 = InstructionSplitterIn[25:21];
  assign Instruction31_26 = InstructionSplitterIn[31:26];
endmodule

module ALUControl (
  input  [5:0] Instruction5_0,
  input  [2:0] ALUOp,
  output [2:0] ALUControlOut,
  output JumpRegister
);

  wire not_1_out, not_2_out, not_3_out, not_4_out, not_5_out;

  Multiplexer #(.select(3), .width(3), .enable("false")) multiplexer_1 (
    .in0(ALUOp), .in1(ALUOp), .in2(ALUOp), .in3(ALUOp), .in4(ALUOp), .in5(ALUOp), .in6(Instruction5_0[2:0]),
    .in7(ALUOp), .out(ALUControlOut), .sel(ALUOp));
  not not_1 (not_1_out, Instruction5_0[0]);
  not not_2 (not_2_out, Instruction5_0[1]);
  not not_3 (not_3_out, Instruction5_0[2]);
  not not_4 (not_4_out, Instruction5_0[4]);
  not not_5 (not_5_out, Instruction5_0[5]);
  and and_1 (JumpRegister, not_1_out, not_2_out, not_3_out, Instruction5_0[3], not_4_out, not_5_out);

  // Notes on the sheet:
  //   Se ALUOp é igual a 110, usa os 3 bits menos significativos da instrução para determinar a operação. Senão, usa ALUOp.
endmodule

module Control (
  input  [5:0] Instruction31_26,
  output [1:0] RegDst,
  output Branch,
  output MemRead,
  output [1:0] MemtoReg,
  output MemWrite,
  output ALUSrc,
  output RegWrite,
  output [1:0] whb,
  output j,
  output [2:0] ALUOp
);

  wire [15:15] rom_1_data;

  ROM #(.addrWidth(6), .dataWidth(16)) rom_1 (
    .addr(Instruction31_26),
    .data({rom_1_data[15], ALUOp, j, MemtoReg[1], RegDst[1], whb, RegWrite, ALUSrc, MemWrite, MemtoReg[0], MemRead, Branch, RegDst[0]}));

  // Notes on the sheet:
  //   contents of rom_1 (hex, n*v repeats v):
  //   6041 0 6800 0 2002 0 0 0 60 0 0 0 4060 5060 0 60 19*0 6c 16c ec 0 0 130 b0 0 30
  //   Se não, ALUControl retorna ALUOp.
  //   Se ALUOp igual 110, ALUControl retorna os 3 bits menos significativos da instrução.
endmodule

module RAMdebug (
  input  [31:0] in_1,
  input  [31:0] in_2,
  input  in_3,
  input  in_4,
  input  [1:0] in_5,
  input  in_6,
  output [31:0] out_7
);

  wire [31:0] register_1_q, register_2_q;

  Register #(.width(32)) register_1 (.D(in_1), .en(1'b1), .clk(in_6), .Q(register_1_q));  // open: clr
  Register #(.width(32)) register_2 (.D(in_2), .en(1'b1), .clk(in_6), .Q(register_2_q));  // open: clr
  Memory memory_1 (
    .Address(register_1_q), .Data(register_2_q), .Write(in_3), .Read(in_4), .whb(in_5), .CLK(in_6),
    .ReadData(out_7));
endmodule

module PCSplitter (
  input  [31:0] PCIn,
  output [3:0] PC31_28
);


  assign PC31_28 = PCIn[31:28];
endmodule

module Joiner (
  input  [31:0] Jump27_0,
  input  [3:0] PC31_28,
  output [31:0] Jump31_0
);


  assign Jump31_0 = {PC31_28, Jump27_0[27:0]};
endmodule
